// Logisim project hw2-flipflop.circ as structural Verilog
module RS_Latch (
  input  S,
  input  R,
  output Q,
  output nQ
);

  nand nand_1 (Q, S, nQ);
  nand nand_2 (nQ, Q, R);
endmodule

// RS
module Clocked_RS_Latch (
  input  S,
  input  R,
  output Q,
  output nQ
);

  wire Ck_out, nand_1_out, nand_2_out;

  Clock Ck (.out(Ck_out));
  nand nand_1 (nand_1_out, S, Ck_out);
  nand nand_2 (nand_2_out, Ck_out, R);
  nand nand_3 (Q, nand_1_out, nQ);
  nand nand_4 (nQ, Q, nand_2_out);
endmodule

module D_flipflop (
  input  D,
  input  CK,
  output Q,
  output nQ
);

  wire not_1_out;

  Clocked_RS_Latch clocked_rs_latch_1 (.S(D), .R(not_1_out), .Q(Q), .nQ(nQ));
  not not_1 (not_1_out, D);
endmodule

module JK_filpflop (
  input  in_1,
  input  J,
  input  K,
  input  in_4,
  output Q,
  output nQ
);

  wire clock_1_out, nand_1_out, nand_2_out;

  Clock clock_1 (.out(clock_1_out));
  nand nand_1 (nand_1_out, in_1, J, clock_1_out);
  nand nand_2 (nand_2_out, clock_1_out, K, in_4);
  nand nand_3 (Q, nand_1_out, nQ);
  nand nand_4 (nQ, Q, nand_2_out);
endmodule
